# Fritzing sketch button (saved by Fritzing 0.9.3b)
perfboards: 1

parts:
  Part1 = Arduino Nano (Rev3.0)
  IC1 = ULN2803A [package=THT]
  R2 = Resistor [tolerance=±5% resistance=10k package=THT]
  DFPlayer_Mini1 = DFPlayer MINI [package="DIP (Dual Inline) [THT]"]
  R1 = Resistor [tolerance=±5% resistance=1k package=THT]
  R3 = Resistor [tolerance=±5% resistance=10k package=THT]
  Part2 = TRRS 3.5mm Jack Breakout
  S1 = Round Pushbutton
  S2 = Round Pushbutton
  LED1 = LED - 5mm [color="Red (633nm)" package="5 mm [THT]"]
  LED2 = LED - 5mm [color="Red (633nm)" package="5 mm [THT]"]

nets:
  N1: Part1.GND, IC1.0V, R2.Pin_0, DFPlayer_Mini1.GND#6, R3.Pin_0, Part2.RING2, S1.leg0, S2.leg0
  N2: Part1.D2, R3.Pin_1, S2.leg1
  N3: Part1.D4, R2.Pin_1, S1.leg1
  N4: Part1.D7, DFPlayer_Mini1.TX
  N5: Part1.D8, R1.Pin_0
  N6: Part1.D12/MISO, IC1.In_2
  N7: Part1.VIN, IC1.COM_-_Common, LED1.anode, LED2.anode
  5V: Part1.5V, DFPlayer_Mini1.VCC
  N8: Part1.D13/SCK, IC1.In_1
  N9: IC1.Out_2, LED1.cathode
  N10: IC1.Out_1, LED2.cathode
  N11: DFPlayer_Mini1.RX, R1.Pin_1
  N12: DFPlayer_Mini1.DAC_R, Part2.RING1
  N13: DFPlayer_Mini1.DAC_L, Part2.TIP

custom parts:
  DFPlayer MINI: MP3 module by DFRobot.com for playing Music from an SD-Card. Supports WAV and MP3 files.
